// Logisim project LABALU.circ as structural Verilog: 14 circuits, main circuit main
module main (
  input  in_1,
  input  in_2,
  input  in_3,
  input  in_4,
  input  [7:0] A,
  input  [7:0] B,
  input  in_7,
  input  in_8,
  input  in_9,
  output [7:0] FINAL,
  output out_11,
  output out_12,
  output out_13
);

  Multiplexor64entradas multiplexor64entradas_1 (
    .ENABLE(in_1), .S0(in_2), .S1(in_3), .S2(in_4), .A(A), .B(B), .RESTAAA(in_7), .SUMAAAA(in_8),
    .MULLTTT(in_9), .SALIDA_FINAL(FINAL), .A_menorque_B(out_11), .OverFlowSuma(out_12),
    .OverFlowMultiplicacion(out_13));
endmodule

module ANDD (
  input  [7:0] A,
  input  [7:0] B,
  output [7:0] out_3
);

  and and_1 (out_3[0], A[0], B[0]);
  and and_2 (out_3[1], A[1], B[1]);
  and and_3 (out_3[2], A[2], B[2]);
  and and_4 (out_3[3], A[3], B[3]);
  and and_5 (out_3[4], A[4], B[4]);
  and and_6 (out_3[5], A[5], B[5]);
  and and_7 (out_3[6], A[6], B[6]);
  and and_8 (out_3[7], A[7], B[7]);
endmodule

module SUMA (
  input  in_1,
  input  [7:0] A,
  input  [7:0] B,
  output [7:0] S,
  output OverflowSuma
);

  wire sum1bit_1_cout, sum1bit_2_cout, sum1bit_3_cout, sum1bit_4_cout, sum1bit_5_cout, sum1bit_6_cout,
       sum1bit_7_cout;

  Sum1bit sum1bit_1 (.A(A[0]), .B(B[0]), .Cin(in_1), .S(S[0]), .Cout(sum1bit_1_cout));
  Sum1bit sum1bit_2 (.A(A[1]), .B(B[1]), .Cin(sum1bit_1_cout), .S(S[1]), .Cout(sum1bit_2_cout));
  Sum1bit sum1bit_3 (.A(A[2]), .B(B[2]), .Cin(sum1bit_2_cout), .S(S[2]), .Cout(sum1bit_3_cout));
  Sum1bit sum1bit_4 (.A(A[3]), .B(B[3]), .Cin(sum1bit_3_cout), .S(S[3]), .Cout(sum1bit_4_cout));
  Sum1bit sum1bit_5 (.A(A[4]), .B(B[4]), .Cin(sum1bit_4_cout), .S(S[4]), .Cout(sum1bit_5_cout));
  Sum1bit sum1bit_6 (.A(A[5]), .B(B[5]), .Cin(sum1bit_5_cout), .S(S[5]), .Cout(sum1bit_6_cout));
  Sum1bit sum1bit_7 (.A(A[6]), .B(B[6]), .Cin(sum1bit_6_cout), .S(S[6]), .Cout(sum1bit_7_cout));
  Sum1bit sum1bit_8 (.A(A[7]), .B(B[7]), .Cin(sum1bit_7_cout), .S(S[7]), .Cout(OverflowSuma));
endmodule

module ORR (
  input  [7:0] A,
  input  [7:0] B,
  output [7:0] out_3
);

  assign out_3 = A | B;  // OR_Gate or_1, 8 bits wide
endmodule

module XORR (
  input  [7:0] A,
  input  [7:0] B,
  output [7:0] out_3
);

  assign out_3 = A ^ B;  // XOR_Gate xor_1, 8 bits wide
endmodule

module NOTT (
  input  [7:0] A,
  output [7:0] out_2
);

  not not_1 (out_2[0], A[0]);
  not not_2 (out_2[1], A[1]);
  not not_3 (out_2[2], A[2]);
  not not_4 (out_2[3], A[3]);
  not not_5 (out_2[4], A[4]);
  not not_6 (out_2[5], A[5]);
  not not_7 (out_2[6], A[6]);
  not not_8 (out_2[7], A[7]);
endmodule

module XNORR (
  input  [7:0] A,
  input  [7:0] B,
  output [7:0] out_3
);

  assign out_3 = ~(A ^ B);  // XNOR_Gate xnor_1, 8 bits wide
endmodule

module RESTA (
  input  in_1,
  input  [7:0] A,
  input  [7:0] B,
  output [7:0] S,
  output A_menor_que_B
);

  wire not_1_out, not_2_out, not_3_out, not_4_out, not_5_out, not_6_out, not_7_out, not_8_out,
       sum1bit_1_cout, sum1bit_2_cout, sum1bit_3_cout, sum1bit_4_cout, sum1bit_5_cout, sum1bit_6_cout,
       sum1bit_7_cout, sum1bit_8_cout;

  not not_1 (not_1_out, B[0]);
  not not_2 (not_2_out, B[1]);
  not not_3 (not_3_out, B[2]);
  not not_4 (not_4_out, B[3]);
  not not_5 (not_5_out, B[4]);
  not not_6 (not_6_out, B[5]);
  not not_7 (not_7_out, B[6]);
  not not_8 (not_8_out, B[7]);
  Sum1bit sum1bit_1 (.A(A[0]), .B(not_1_out), .Cin(in_1), .S(S[0]), .Cout(sum1bit_1_cout));
  Sum1bit sum1bit_2 (.A(A[1]), .B(not_2_out), .Cin(sum1bit_1_cout), .S(S[1]), .Cout(sum1bit_2_cout));
  Sum1bit sum1bit_3 (.A(A[2]), .B(not_3_out), .Cin(sum1bit_2_cout), .S(S[2]), .Cout(sum1bit_3_cout));
  Sum1bit sum1bit_4 (.A(A[3]), .B(not_4_out), .Cin(sum1bit_3_cout), .S(S[3]), .Cout(sum1bit_4_cout));
  Sum1bit sum1bit_5 (.A(A[4]), .B(not_5_out), .Cin(sum1bit_4_cout), .S(S[4]), .Cout(sum1bit_5_cout));
  Sum1bit sum1bit_6 (.A(A[5]), .B(not_6_out), .Cin(sum1bit_5_cout), .S(S[5]), .Cout(sum1bit_6_cout));
  Sum1bit sum1bit_7 (.A(A[6]), .B(not_7_out), .Cin(sum1bit_6_cout), .S(S[6]), .Cout(sum1bit_7_cout));
  Sum1bit sum1bit_8 (.A(A[7]), .B(not_8_out), .Cin(sum1bit_7_cout), .S(S[7]), .Cout(sum1bit_8_cout));
  not not_9 (A_menor_que_B, sum1bit_8_cout);
endmodule

module MULTIPLICACION (
  input  in_1,
  input  [7:0] A,
  input  [7:0] B,
  output [7:0] ResultadoMultiplicacion,
  output OverFlowMulti
);

  wire suma_1_overflowsuma, suma_2_overflowsuma, suma_3_overflowsuma, suma_4_overflowsuma,
       suma_5_overflowsuma, suma_6_overflowsuma, suma_7_overflowsuma;
  wire [7:0] minimultiplicador_1_out_3, minimultiplicador_2_out_3, minimultiplicador_3_out_3,
       minimultiplicador_4_out_3, minimultiplicador_5_out_3, minimultiplicador_6_out_3,
       minimultiplicador_7_out_3, minimultiplicador_8_out_3, suma_1_s, suma_2_s, suma_3_s, suma_4_s,
       suma_5_s, suma_6_s;

  miniMultiplicador minimultiplicador_1 (.A(A), .B(B[0]), .out_3(minimultiplicador_1_out_3));
  miniMultiplicador minimultiplicador_2 (.A(A), .B(B[1]), .out_3(minimultiplicador_2_out_3));
  miniMultiplicador minimultiplicador_3 (.A(A), .B(B[2]), .out_3(minimultiplicador_3_out_3));
  miniMultiplicador minimultiplicador_4 (.A(A), .B(B[3]), .out_3(minimultiplicador_4_out_3));
  miniMultiplicador minimultiplicador_5 (.A(A), .B(B[4]), .out_3(minimultiplicador_5_out_3));
  miniMultiplicador minimultiplicador_6 (.A(A), .B(B[5]), .out_3(minimultiplicador_6_out_3));
  miniMultiplicador minimultiplicador_7 (.A(A), .B(B[6]), .out_3(minimultiplicador_7_out_3));
  miniMultiplicador minimultiplicador_8 (.A(A), .B(B[7]), .out_3(minimultiplicador_8_out_3));
  SUMA suma_1 (
    .in_1(in_1), .A(minimultiplicador_1_out_3), .B({minimultiplicador_2_out_3[6:0], in_1}), .S(suma_1_s),
    .OverflowSuma(suma_1_overflowsuma));
  SUMA suma_2 (
    .in_1(in_1), .A({minimultiplicador_3_out_3[5:0], {2{in_1}}}),
    .B({minimultiplicador_4_out_3[4:0], {3{in_1}}}), .S(suma_2_s), .OverflowSuma(suma_2_overflowsuma));
  SUMA suma_3 (
    .in_1(in_1), .A({minimultiplicador_5_out_3[3:0], {4{in_1}}}),
    .B({minimultiplicador_6_out_3[2:0], {5{in_1}}}), .S(suma_3_s), .OverflowSuma(suma_3_overflowsuma));
  SUMA suma_4 (
    .in_1(in_1), .A({minimultiplicador_7_out_3[1:0], {6{in_1}}}),
    .B({minimultiplicador_8_out_3[0], {7{in_1}}}), .S(suma_4_s), .OverflowSuma(suma_4_overflowsuma));
  SUMA suma_5 (.in_1(in_1), .A(suma_1_s), .B(suma_2_s), .S(suma_5_s), .OverflowSuma(suma_5_overflowsuma));
  SUMA suma_6 (.in_1(in_1), .A(suma_3_s), .B(suma_4_s), .S(suma_6_s), .OverflowSuma(suma_6_overflowsuma));
  SUMA suma_7 (
    .in_1(in_1), .A(suma_5_s), .B(suma_6_s), .S(ResultadoMultiplicacion), .OverflowSuma(suma_7_overflowsuma));
  or or_1 (OverFlowMulti, suma_7_overflowsuma, suma_5_overflowsuma, suma_6_overflowsuma, suma_1_overflowsuma, suma_2_overflowsuma, suma_3_overflowsuma, suma_4_overflowsuma);
endmodule

module Sum1bit (
  input  A,
  input  B,
  input  Cin,
  output S,
  output Cout
);

  wire and_1_out, and_2_out, and_3_out, or_1_out, xor_1_out;

  xor xor_1 (xor_1_out, Cin, B);
  and and_1 (and_1_out, B, Cin);
  and and_2 (and_2_out, A, Cin);
  xor xor_2 (S, xor_1_out, A);
  or or_1 (or_1_out, and_1_out, and_2_out);
  and and_3 (and_3_out, A, B);
  or or_2 (Cout, or_1_out, and_3_out);
endmodule

module Multiplexor64entradas (
  input  ENABLE,
  input  S0,
  input  S1,
  input  S2,
  input  [7:0] A,
  input  [7:0] B,
  input  RESTAAA,
  input  SUMAAAA,
  input  MULLTTT,
  output [7:0] SALIDA_FINAL,
  output A_menorque_B,
  output OverFlowSuma,
  output OverFlowMultiplicacion
);

  wire [7:0] andd_1_out_3, multiplicacion_1_resultadomultiplicacion, nott_1_out_2, orr_1_out_3, resta_1_s,
       suma_1_s, xnorr_1_out_3, xorr_1_out_3;

  ANDD andd_1 (.A(A), .B(B), .out_3(andd_1_out_3));
  ORR orr_1 (.A(A), .B(B), .out_3(orr_1_out_3));
  XORR xorr_1 (.A(A), .B(B), .out_3(xorr_1_out_3));
  NOTT nott_1 (.A(A), .out_2(nott_1_out_2));
  XNORR xnorr_1 (.A(A), .B(B), .out_3(xnorr_1_out_3));
  RESTA resta_1 (
    .in_1(RESTAAA), .A(A), .B(B), .S({resta_1_s[7:5], resta_1_s[5], resta_1_s[3:0]}),
    .A_menor_que_B(A_menorque_B));
  SUMA suma_1 (.in_1(SUMAAAA), .A(A), .B(B), .S(suma_1_s), .OverflowSuma(OverFlowSuma));
  MULTIPLICACION multiplicacion_1 (
    .in_1(MULLTTT), .A(A), .B(B), .ResultadoMultiplicacion(multiplicacion_1_resultadomultiplicacion),
    .OverFlowMulti(OverFlowMultiplicacion));
  Mux8_prueba mux8_prueba_1 (
    .S1(S1), .S2(S2), .S0(S0), .ENABLE(ENABLE), .I0(andd_1_out_3[0]), .I1(orr_1_out_3[0]),
    .I2(xorr_1_out_3[0]), .I3(nott_1_out_2[0]), .I4(xnorr_1_out_3[0]), .I5(resta_1_s[0]), .I6(suma_1_s[0]),
    .I7(multiplicacion_1_resultadomultiplicacion[0]), .Z(SALIDA_FINAL[0]));
  Mux8_prueba mux8_prueba_2 (
    .S1(S1), .S2(S2), .S0(S0), .ENABLE(ENABLE), .I0(andd_1_out_3[1]), .I1(orr_1_out_3[1]),
    .I2(xorr_1_out_3[1]), .I3(nott_1_out_2[1]), .I4(xnorr_1_out_3[1]), .I5(resta_1_s[1]), .I6(suma_1_s[1]),
    .I7(multiplicacion_1_resultadomultiplicacion[1]), .Z(SALIDA_FINAL[1]));
  Mux8_prueba mux8_prueba_3 (
    .S1(S1), .S2(S2), .S0(S0), .ENABLE(ENABLE), .I0(andd_1_out_3[2]), .I1(orr_1_out_3[2]),
    .I2(xorr_1_out_3[2]), .I3(nott_1_out_2[2]), .I4(xnorr_1_out_3[2]), .I5(resta_1_s[2]), .I6(suma_1_s[2]),
    .I7(multiplicacion_1_resultadomultiplicacion[2]), .Z(SALIDA_FINAL[2]));
  Mux8_prueba mux8_prueba_4 (
    .S1(S1), .S2(S2), .S0(S0), .ENABLE(ENABLE), .I0(andd_1_out_3[3]), .I1(orr_1_out_3[3]),
    .I2(xorr_1_out_3[3]), .I3(nott_1_out_2[3]), .I4(xnorr_1_out_3[3]), .I5(resta_1_s[3]), .I6(suma_1_s[3]),
    .I7(multiplicacion_1_resultadomultiplicacion[3]), .Z(SALIDA_FINAL[3]));
  Mux8_prueba mux8_prueba_5 (
    .S1(S1), .S2(S2), .S0(S0), .ENABLE(ENABLE), .I0(andd_1_out_3[4]), .I1(orr_1_out_3[4]),
    .I2(xorr_1_out_3[4]), .I3(nott_1_out_2[4]), .I4(xnorr_1_out_3[4]), .I5(resta_1_s[5]), .I6(suma_1_s[4]),
    .I7(multiplicacion_1_resultadomultiplicacion[4]), .Z(SALIDA_FINAL[4]));
  Mux8_prueba mux8_prueba_6 (
    .S1(S1), .S2(S2), .S0(S0), .ENABLE(ENABLE), .I0(andd_1_out_3[5]), .I1(orr_1_out_3[5]),
    .I2(xorr_1_out_3[5]), .I3(nott_1_out_2[5]), .I4(xnorr_1_out_3[5]), .I5(resta_1_s[5]), .I6(suma_1_s[5]),
    .I7(multiplicacion_1_resultadomultiplicacion[5]), .Z(SALIDA_FINAL[5]));
  Mux8_prueba mux8_prueba_7 (
    .S1(S1), .S2(S2), .S0(S0), .ENABLE(ENABLE), .I0(andd_1_out_3[6]), .I1(orr_1_out_3[6]),
    .I2(xorr_1_out_3[6]), .I3(nott_1_out_2[6]), .I4(xnorr_1_out_3[6]), .I5(resta_1_s[6]), .I6(suma_1_s[6]),
    .I7(multiplicacion_1_resultadomultiplicacion[6]), .Z(SALIDA_FINAL[6]));
  Mux8_prueba mux8_prueba_8 (
    .S1(S1), .S2(S2), .S0(S0), .ENABLE(ENABLE), .I0(andd_1_out_3[7]), .I1(orr_1_out_3[7]),
    .I2(xorr_1_out_3[7]), .I3(nott_1_out_2[7]), .I4(xnorr_1_out_3[7]), .I5(resta_1_s[7]), .I6(suma_1_s[7]),
    .I7(multiplicacion_1_resultadomultiplicacion[7]), .Z(SALIDA_FINAL[7]));
endmodule

module miniMultiplicador (
  input  [7:0] A,
  input  B,
  output [7:0] out_3
);

  and and_1 (out_3[0], A[0], B);
  and and_2 (out_3[1], A[1], B);
  and and_3 (out_3[2], A[2], B);
  and and_4 (out_3[3], A[3], B);
  and and_5 (out_3[4], A[4], B);
  and and_6 (out_3[5], A[5], B);
  and and_7 (out_3[6], A[6], B);
  and and_8 (out_3[7], A[7], B);
endmodule

module mux_2a_1bit (
  input  S,
  input  I0,
  input  I1,
  output Z
);

  wire and_1_out, and_2_out, not_1_out;

  not not_1 (not_1_out, S);
  and and_1 (and_1_out, not_1_out, I0);
  and and_2 (and_2_out, S, I1);
  or or_1 (Z, and_1_out, and_2_out);
endmodule

module Mux8_prueba (
  input  S1,
  input  S2,
  input  S0,
  input  ENABLE,
  input  I0,
  input  I1,
  input  I2,
  input  I3,
  input  I4,
  input  I5,
  input  I6,
  input  I7,
  output Z
);

  wire mux_2a_1bit_1_z, mux_2a_1bit_2_z, mux_2a_1bit_3_z, mux_2a_1bit_4_z, mux_2a_1bit_5_z, mux_2a_1bit_6_z,
       mux_2a_1bit_7_z;

  mux_2a_1bit mux_2a_1bit_1 (.S(S0), .I0(I0), .I1(I1), .Z(mux_2a_1bit_1_z));
  mux_2a_1bit mux_2a_1bit_2 (.S(S0), .I0(I2), .I1(I3), .Z(mux_2a_1bit_2_z));
  mux_2a_1bit mux_2a_1bit_3 (.S(S0), .I0(I4), .I1(I5), .Z(mux_2a_1bit_3_z));
  mux_2a_1bit mux_2a_1bit_4 (.S(S0), .I0(I6), .I1(I7), .Z(mux_2a_1bit_4_z));
  mux_2a_1bit mux_2a_1bit_5 (.S(S1), .I0(mux_2a_1bit_1_z), .I1(mux_2a_1bit_2_z), .Z(mux_2a_1bit_5_z));
  mux_2a_1bit mux_2a_1bit_6 (.S(S1), .I0(mux_2a_1bit_3_z), .I1(mux_2a_1bit_4_z), .Z(mux_2a_1bit_6_z));
  mux_2a_1bit mux_2a_1bit_7 (.S(S2), .I0(mux_2a_1bit_5_z), .I1(mux_2a_1bit_6_z), .Z(mux_2a_1bit_7_z));
  and and_1 (Z, ENABLE, mux_2a_1bit_7_z);
endmodule
